// Digital circuit sim_control_bomba.dig as structural Verilog
module sim_control_bomba (
  input  Ck,
  input  Ck_controlador
);

  wire Bomba_de_Agua_p4, bombaConAgua, C_out, cisternaL, cisternaOK, Controlador_de_Bomba_de_Agua_bomba,
       I_out, L_out, M_out, or_1_out, rs_ff_as_1_q, tanqueMaximo, tanqueMinimo, U_out;
  wire [9:0] Tanque_p4;
  wire [19:0] Cisterna_p4;

  control_bomba Controlador_de_Bomba_de_Agua (
    .tanqueH(tanqueMaximo), .tanqueL(tanqueMinimo), .cisternaOK(cisternaOK), .cisternaL(cisternaL),
    .Ck(Ck_controlador), .bomba(Controlador_de_Bomba_de_Agua_bomba));
  or or_1 (or_1_out, M_out, Controlador_de_Bomba_de_Agua_bomba);
  Button M (.out(M_out));
  Button C (.out(C_out));
  // bomba Bomba_de_Agua: pin names not known; wires that end beside it: or_1_out, bombaConAgua, C_out, Bomba_de_Agua_p4
  Button U (.out(U_out));
  Button I (.out(I_out));
  // tanque #(.generic("bits:=10;")) Tanque: pin names not known; wires that end beside it: Bomba_de_Agua_p4, U_out, Ck, {Tanque_p4[9], tanqueMaximo, Tanque_p4[7:2], tanqueMinimo, Tanque_p4[0]}
  // tanque #(.generic("bits:=20;")) Cisterna: pin names not known; wires that end beside it: I_out, Bomba_de_Agua_p4, Ck, {Cisterna_p4[19:6], cisternaOK, Cisterna_p4[4], cisternaL, bombaConAgua, Cisterna_p4[1:0]}
  Button L (.out(L_out));
  RS_FF_AS rs_ff_as_1 (.S(Tanque_p4[9]), .R(L_out), .Q(rs_ff_as_1_q));  // open: nQ
  LED led_1 (.in(Tanque_p4[9]));
  LED led_2 (.in(tanqueMaximo));
  LED led_3 (.in(Tanque_p4[7]));
  LED led_4 (.in(Tanque_p4[6]));
  LED led_5 (.in(Tanque_p4[5]));
  LED led_6 (.in(Tanque_p4[4]));
  LED led_7 (.in(Tanque_p4[3]));
  LED led_8 (.in(Tanque_p4[2]));
  LED led_9 (.in(tanqueMinimo));
  LED led_10 (.in(Tanque_p4[0]));
  LED led_11 (.in(Cisterna_p4[19]));
  LED led_12 (.in(Cisterna_p4[17]));
  LED led_13 (.in(Cisterna_p4[15]));
  LED led_14 (.in(Cisterna_p4[13]));
  LED led_15 (.in(Cisterna_p4[11]));
  LED led_16 (.in(Cisterna_p4[9]));
  LED led_17 (.in(Cisterna_p4[7]));
  LED led_18 (.in(cisternaOK));
  LED led_19 (.in(cisternaL));
  LED led_20 (.in(Cisterna_p4[1]));
  LED Derramado (.in(rs_ff_as_1_q));

  // Notes on the sheet:
  //   Ck: Hz: 4
  //   Ck_controlador: Hz: 8
  //   Simulador de control de bomba
  //   ==========================
  //   Durante la simulación las columnas
  //   de LED indican los niveles del tanque de
  //   agua (superior) y la cisterna (inferior).
  //   El led grande indica que se ha derramado
  //   agua y debe limpiarse. Este LED solo se
  //   apagará si se limpia el agua cuando el
  //   tanque no está rebalzando.
  //   Si la bomba funciona cuando es bajo el nivel
  //   de la cisterna (está apagado el penúltimo LED),
  //   la misma se descebará y dejará de funcionar
  //   (no se llenará el tanque). Para solucionarlo
  //   debemos cebarla (solo cuando la cisterna tiene
  //   nivel adecuado, dos LED).
  //   Durante la simulación presiona
  //   'i' para llenar la cisterna
  //   'u' para vaciar el tanque
  //   'm' para encender la bomba en forma manual
  //   'L' para limpiar el derrame de agua (el ultimo
  //   LED del tanque indica si está aún rebalsando)
  //   'c' para cebar la bomba (solo cuando hay suficiente
  //   agua en la cisterna, de lo contrario se descebará
  //   de inmediato)
endmodule
